# Fritzing sketch slave (saved by Fritzing 0.9.4)
breadboards: 1

parts:
  Bauteil1 = Arduino Nano (Rev3.0) (ICSP)
  Grove1 = Grove 4 Digit Display
  Grove2 = Grove 4 Digit Display
  Bauteil2 = NRF24L01+ Breakout Board
  LED1 = smd LED [color="Red (633nm)" package="1206 [SMD]"]
  LED2 = smd LED [color="Yellow (595nm)" package="1206 [SMD]"]
  LED3 = smd LED [color="Green (555nm)" package="1206 [SMD]"]
  SP1 = SPEAKER [package=pcb_mount_speaker]
  R1 = Resistor [tolerance=±5% resistance=220 package=THT]
  R2 = Resistor [tolerance=±5% resistance=220 package=THT]
  R3 = Resistor [tolerance=±5% resistance=220 package=THT]

nets:
  GND: Bauteil1.GND, Grove1.GND, Grove2.GND, Bauteil2.GND, LED1.cathode, LED2.cathode, LED3.cathode, SP1.+
  N1: Bauteil1.D2, Grove1.CLK, Grove2.CLK
  N2: Bauteil1.D3, Grove2.DIO
  N3: Bauteil1.D4, Grove1.DIO
  N4: Bauteil1.D5, SP1.-
  N5: Bauteil1.D6, Bauteil2.CE
  N6: Bauteil1.D7, Bauteil2.CS
  N7: Bauteil1.D8, R1.Pin_0
  N8: Bauteil1.D9, R2.Pin_0
  N9: Bauteil1.D10, R3.Pin_0
  N10: Bauteil1.D11/MOSI, Bauteil2.MOSI
  N11: Bauteil1.D12/MISO, Bauteil2.MISO
  VCC: Bauteil1.5V, Grove1.VCC, Grove2.VCC
  3V3: Bauteil1.3V3, Bauteil2.VCC
  N12: Bauteil1.D13/SCK, Bauteil2.SCK
  N13: LED1.anode, R1.Pin_1
  N14: LED2.anode, R3.Pin_1
  N15: LED3.anode, R2.Pin_1
